// Logisim project 4-bit-ALU.circ as structural Verilog: 1 circuit, main circuit main
module main (
  input  [3:0] A,
  input  [3:0] B,
  input  [2:0] Selector,
  output [3:0] out_4
);

  wire [3:0] adder_1_out;

  Adder #(.width(4)) adder_1 (.a(A), .b(B), .out(adder_1_out));  // open: cin, cout
  Multiplexer #(.select(3), .width(4)) multiplexer_1 (
    .in0(adder_1_out), .out(out_4), .sel(Selector));  // open: in1, in2, in3, in4, in5, in6, in7, en

  // Notes on the sheet:
  //   Out Put
endmodule
